// Logisim project sCPU_1.circ as structural Verilog: 23 circuits, main circuit main
module main (
  input  in_1
);

  wire and_1_out, and_2_out, and_3_out, and_4_out, clock_1_out, decoder2_4_1_out_3, decoder2_4_1_out_5,
       decoder2_4_1_out_6, decoder2_4_2_out_3, decoder2_4_2_out_4, decoder2_4_2_out_5, decoder2_4_2_out_6,
       decoder3_8_1_out_4, or_9_out, small_and_1_out_3, small_and_2_out_3, small_and_3_out_3,
       small_and_4_out_3, small_and_5_out_3, small_and_6_out_3, small_and_7_out_3, small_and_8_out_3;
  wire [1:0] or_2_out, or_3_out;
  wire [3:0] or_8_out;
  wire [7:0] counter_8bits_1_out_3, immidiate_expansion_1_out_2, register_8bits_en_1_out_4,
       register_8bits_en_2_out_4, register_8bits_en_3_out_4, register_8bits_en_4_out_4;

  Clock clock_1 (.out(clock_1_out));
  small_and small_and_1 (.in_1(decoder3_8_1_out_4), .in_2(1'b1), .out_3(small_and_1_out_3));
  buf or_1 (or_2_out[1], small_and_1_out_3);  // OR_Gate
  small_and small_and_2 (.in_1(decoder3_8_1_out_4), .in_2(1'b0), .out_3(small_and_2_out_3));
  DECODER2_4 decoder2_4_1 (
    .in_2(or_2_out[1]), .B(or_2_out[0]), .out_3(decoder2_4_1_out_3), .out_5(decoder2_4_1_out_5),
    .out_6(decoder2_4_1_out_6));  // open: out_4
  buf or_2 (or_2_out[0], small_and_2_out_3);  // OR_Gate
  small_and small_and_3 (.in_1(decoder3_8_1_out_4), .in_2(1'b0), .out_3(small_and_3_out_3));
  buf or_3 (or_3_out[0], small_and_3_out_3);  // OR_Gate
  counter_8bits counter_8bits_1 (.in_1(in_1), .in_2(clock_1_out), .out_3(counter_8bits_1_out_3));
  small_and small_and_4 (.in_1(decoder3_8_1_out_4), .in_2(1'b0), .out_3(small_and_4_out_3));
  buf or_4 (or_3_out[1], small_and_4_out_3);  // OR_Gate
  small_and small_and_5 (.in_1(decoder3_8_1_out_4), .in_2(1'b1), .out_3(small_and_5_out_3));
  buf or_5 (or_8_out[3], small_and_5_out_3);  // OR_Gate
  small_and small_and_6 (.in_1(decoder3_8_1_out_4), .in_2(1'b1), .out_3(small_and_6_out_3));
  buf or_6 (or_8_out[2], small_and_6_out_3);  // OR_Gate
  small_and small_and_7 (.in_1(decoder3_8_1_out_4), .in_2(1'b1), .out_3(small_and_7_out_3));
  buf or_7 (or_8_out[1], small_and_7_out_3);  // OR_Gate
  decoder3_8 decoder3_8_1 (
    .in_1(counter_8bits_1_out_3[0]), .in_2(counter_8bits_1_out_3[1]), .in_3(counter_8bits_1_out_3[2]),
    .out_4(decoder3_8_1_out_4));  // open: out_5, out_6, out_7, out_8, out_9, out_10, out_11
  small_and small_and_8 (.in_1(decoder3_8_1_out_4), .in_2(1'b0), .out_3(small_and_8_out_3));
  buf or_8 (or_8_out[0], small_and_8_out_3);  // OR_Gate
  or or_9 (or_9_out, decoder2_4_1_out_3, decoder2_4_1_out_5);
  immidiate_expansion immidiate_expansion_1 (
    .in_1({or_8_out[2], or_8_out[3], or_8_out[1:0]}), .out_2(immidiate_expansion_1_out_2));
  DECODER2_4 decoder2_4_2 (
    .in_2(or_3_out[1]), .B(or_3_out[0]), .out_3(decoder2_4_2_out_3), .out_4(decoder2_4_2_out_4),
    .out_5(decoder2_4_2_out_5), .out_6(decoder2_4_2_out_6));
  and and_1 (and_1_out, or_9_out, decoder2_4_2_out_3);
  and and_2 (and_2_out, or_9_out, decoder2_4_2_out_4);
  and and_3 (and_3_out, or_9_out, decoder2_4_2_out_5);
  and and_4 (and_4_out, or_9_out, decoder2_4_2_out_6);
  register_8bits_en register_8bits_en_1 (
    .in_3(immidiate_expansion_1_out_2), .in_2(clock_1_out), .in_1(and_1_out),
    .out_4(register_8bits_en_1_out_4));
  register_8bits_en register_8bits_en_2 (
    .in_3(immidiate_expansion_1_out_2), .in_2(clock_1_out), .in_1(and_2_out),
    .out_4(register_8bits_en_2_out_4));
  register_8bits_en register_8bits_en_3 (
    .in_3(immidiate_expansion_1_out_2), .in_2(clock_1_out), .in_1(and_3_out),
    .out_4(register_8bits_en_3_out_4));
  register_8bits_en register_8bits_en_4 (
    .in_3(immidiate_expansion_1_out_2), .in_2(clock_1_out), .in_1(and_4_out),
    .out_4(register_8bits_en_4_out_4));

  // Notes on the sheet:
  //   ROM_8*8
  //   Decoder
  //   opcode
  //   add
  //   li
  //   bner0
  //   PC
  //   ROM_8*8
  //   imm
  //   rs2
  //   rs1
  //   branch_address
  //   Write_address(rd)
  //   Write_enable
  //   Write_Enable
  //   write_decoder
  //   Register_file
endmodule

module MUX2 (
  input  in_1,
  input  in_2,
  input  in_3,
  output out_4
);

  wire not_1_out;

  not not_1 (not_1_out, in_1);
  // Transmission_Gate transmission_1: pin names not known; wires that end beside it: in_2, in_1, not_1_out, out_4
  // Transmission_Gate transmission_2: pin names not known; wires that end beside it: in_3, not_1_out, in_1, out_4
endmodule

module SR_Latch (
  input  in_1,
  input  in_2,
  output out_3
);

  wire nor_1_out;

  nor nor_1 (nor_1_out, in_1, out_3);
  nor nor_2 (out_3, nor_1_out, in_2);

  // Notes on the sheet:
  //   Q_
endmodule

module D_Latch (
  input  in_1,
  input  in_2,
  output out_3
);

  wire and_1_out, and_2_out, not_1_out;

  not not_1 (not_1_out, in_1);
  and and_1 (and_1_out, in_1, in_2);
  and and_2 (and_2_out, in_2, not_1_out);
  SR_Latch sr_latch_1 (.in_2(and_2_out), .in_1(and_1_out), .out_3(out_3));

  // Notes on the sheet:
  //   Q
endmodule

module D_FF (
  input  in_1,
  input  in_2,
  output out_3
);

  wire d_latch_1_out_3, not_1_out;

  not not_1 (not_1_out, in_2);
  D_Latch d_latch_1 (.in_2(not_1_out), .in_1(in_1), .out_3(d_latch_1_out_3));
  D_Latch d_latch_2 (.in_2(in_2), .in_1(d_latch_1_out_3), .out_3(out_3));

  // Notes on the sheet:
  //   RST
endmodule

module D_FF_rst (
  input  in_1,
  input  in_2,
  input  in_3,
  output out_4
);

  wire and_1_out, d_latch_1_out_3, not_1_out, not_2_out;

  not not_1 (not_1_out, in_1);
  not not_2 (not_2_out, in_3);
  and and_1 (and_1_out, not_1_out, in_2);
  D_Latch d_latch_1 (.in_2(not_2_out), .in_1(and_1_out), .out_3(d_latch_1_out_3));
  D_Latch d_latch_2 (.in_2(in_3), .in_1(d_latch_1_out_3), .out_3(out_4));
endmodule

module D_FF_EN (
  input  in_1,
  input  EN,
  input  in_3,
  output out_4
);

  wire and_1_out;

  and and_1 (and_1_out, EN, in_3);
  D_FF d_ff_1 (.in_1(in_1), .in_2(and_1_out), .out_3(out_4));
endmodule

module register_8bits (
  input  in_1,
  input  in_2,
  input  [7:0] in_3,
  output [7:0] out_4
);

  D_FF_rst d_ff_rst_1 (.in_1(in_1), .in_2(in_3[0]), .in_3(in_2), .out_4(out_4[0]));
  D_FF_rst d_ff_rst_2 (.in_1(in_1), .in_2(in_3[1]), .in_3(in_2), .out_4(out_4[1]));
  D_FF_rst d_ff_rst_3 (.in_1(in_1), .in_2(in_3[2]), .in_3(in_2), .out_4(out_4[2]));
  D_FF_rst d_ff_rst_4 (.in_1(in_1), .in_2(in_3[3]), .in_3(in_2), .out_4(out_4[3]));
  D_FF_rst d_ff_rst_5 (.in_1(in_1), .in_2(in_3[4]), .in_3(in_2), .out_4(out_4[4]));
  D_FF_rst d_ff_rst_6 (.in_1(in_1), .in_2(in_3[5]), .in_3(in_2), .out_4(out_4[5]));
  D_FF_rst d_ff_rst_7 (.in_1(in_1), .in_2(in_3[6]), .in_3(in_2), .out_4(out_4[6]));
  D_FF_rst d_ff_rst_8 (.in_1(in_1), .in_2(in_3[7]), .in_3(in_2), .out_4(out_4[7]));
endmodule

module DECODER2_4 (
  input  B,
  input  in_2,
  output out_3,
  output out_4,
  output out_5,
  output out_6
);

  wire not_1_out, not_2_out, not_3_out;

  not not_1 (not_1_out, in_2);
  not not_2 (not_2_out, B);
  not not_3 (not_3_out, B);
  and and_1 (out_3, not_1_out, not_2_out);
  and and_2 (out_4, not_1_out, B);
  and and_3 (out_5, in_2, not_3_out);
  and and_4 (out_6, in_2, B);

  // Notes on the sheet:
  //   A
endmodule

module decoder3_8 (
  input  in_1,
  input  in_2,
  input  in_3,
  output out_4,
  output out_5,
  output out_6,
  output out_7,
  output out_8,
  output out_9,
  output out_10,
  output out_11
);

  wire not_1_out, not_2_out, not_3_out;

  not not_1 (not_1_out, in_1);
  not not_2 (not_2_out, in_2);
  not not_3 (not_3_out, in_3);
  and and_1 (out_4, not_1_out, not_2_out, not_3_out);
  and and_2 (out_5, in_1, not_2_out, not_3_out);
  and and_3 (out_6, not_1_out, in_2, not_3_out);
  and and_4 (out_7, in_1, in_2, not_3_out);
  and and_5 (out_8, not_1_out, not_2_out, in_3);
  and and_6 (out_9, in_1, not_2_out, in_3);
  and and_7 (out_10, not_1_out, in_2, in_3);
  and and_8 (out_11, in_1, in_2, in_3);
endmodule

module register_8bits_en (
  input  in_1,
  input  in_2,
  input  [7:0] in_3,
  output [7:0] out_4
);

  D_FF_EN d_ff_en_1 (.EN(in_1), .in_1(in_3[0]), .in_3(in_2), .out_4(out_4[0]));
  D_FF_EN d_ff_en_2 (.EN(in_1), .in_1(in_3[1]), .in_3(in_2), .out_4(out_4[1]));
  D_FF_EN d_ff_en_3 (.EN(in_1), .in_1(in_3[2]), .in_3(in_2), .out_4(out_4[2]));
  D_FF_EN d_ff_en_4 (.EN(in_1), .in_1(in_3[3]), .in_3(in_2), .out_4(out_4[3]));
  D_FF_EN d_ff_en_5 (.EN(in_1), .in_1(in_3[4]), .in_3(in_2), .out_4(out_4[4]));
  D_FF_EN d_ff_en_6 (.EN(in_1), .in_1(in_3[5]), .in_3(in_2), .out_4(out_4[5]));
  D_FF_EN d_ff_en_7 (.EN(in_1), .in_1(in_3[6]), .in_3(in_2), .out_4(out_4[6]));
  D_FF_EN d_ff_en_8 (.EN(in_1), .in_1(in_3[7]), .in_3(in_2), .out_4(out_4[7]));
endmodule

module decoder4_16 (
  input  in_1,
  input  in_2,
  input  in_3,
  input  in_4,
  output out_5,
  output out_6,
  output out_7,
  output out_8,
  output out_9,
  output out_10,
  output out_11,
  output out_12,
  output out_13,
  output out_14,
  output out_15,
  output out_16,
  output out_17,
  output out_18,
  output out_19,
  output out_20
);

  wire and_1_out, and_2_out, and_3_out, and_4_out, and_5_out, and_6_out, decoder3_8_1_out_4,
       decoder3_8_2_out_4, not_1_out;

  not not_1 (not_1_out, in_4);
  and and_1 (and_1_out, in_1, not_1_out);
  and and_2 (and_2_out, in_2, not_1_out);
  and and_3 (and_3_out, in_3, not_1_out);
  and and_4 (and_4_out, in_4, in_1);
  and and_5 (and_5_out, in_4, in_2);
  and and_6 (and_6_out, in_4, in_3);
  decoder3_8 decoder3_8_1 (
    .in_1(and_1_out), .in_2(and_2_out), .in_3(and_3_out), .out_4(decoder3_8_1_out_4), .out_5(out_6),
    .out_6(out_7), .out_7(out_8), .out_8(out_9), .out_9(out_10), .out_10(out_11), .out_11(out_12));
  decoder3_8 decoder3_8_2 (
    .in_1(and_4_out), .in_2(and_5_out), .in_3(and_6_out), .out_4(decoder3_8_2_out_4), .out_5(out_14),
    .out_6(out_15), .out_7(out_16), .out_8(out_17), .out_9(out_18), .out_10(out_19), .out_11(out_20));
  and and_7 (out_5, not_1_out, decoder3_8_1_out_4);
  and and_8 (out_13, in_4, decoder3_8_2_out_4);
endmodule

module decoder_7segments_i (
  input  in_1,
  input  in_2,
  input  in_3,
  input  in_4,
  output out_5,
  output out_6,
  output out_7,
  output out_8,
  output out_9,
  output out_10,
  output out_11
);

  wire button_1_out, button_2_out, button_3_out, button_4_out, button_5_out, button_6_out, button_7_out,
       button_8_out, decoder4_16_1_out_5, decoder4_16_1_out_6, decoder4_16_1_out_7, decoder4_16_1_out_8,
       decoder4_16_1_out_9, decoder4_16_1_out_10, decoder4_16_1_out_11, decoder4_16_1_out_12,
       decoder4_16_1_out_13, decoder4_16_1_out_14, decoder4_16_1_out_15, decoder4_16_1_out_16,
       decoder4_16_1_out_17, decoder4_16_1_out_18, decoder4_16_1_out_19, decoder4_16_1_out_20;

  decoder4_16 decoder4_16_1 (
    .in_1(in_1), .in_2(in_2), .in_3(in_3), .in_4(in_4), .out_5(decoder4_16_1_out_5),
    .out_6(decoder4_16_1_out_6), .out_7(decoder4_16_1_out_7), .out_8(decoder4_16_1_out_8),
    .out_9(decoder4_16_1_out_9), .out_10(decoder4_16_1_out_10), .out_11(decoder4_16_1_out_11),
    .out_12(decoder4_16_1_out_12), .out_13(decoder4_16_1_out_13), .out_14(decoder4_16_1_out_14),
    .out_15(decoder4_16_1_out_15), .out_16(decoder4_16_1_out_16), .out_17(decoder4_16_1_out_17),
    .out_18(decoder4_16_1_out_18), .out_19(decoder4_16_1_out_19), .out_20(decoder4_16_1_out_20));
  or or_1 (out_5, decoder4_16_1_out_7, decoder4_16_1_out_8, decoder4_16_1_out_9, decoder4_16_1_out_10, decoder4_16_1_out_11, decoder4_16_1_out_13, decoder4_16_1_out_14, decoder4_16_1_out_15, decoder4_16_1_out_16, decoder4_16_1_out_18, decoder4_16_1_out_19, decoder4_16_1_out_20);
  or or_2 (out_6, decoder4_16_1_out_5, decoder4_16_1_out_9, decoder4_16_1_out_10, decoder4_16_1_out_11, decoder4_16_1_out_13, decoder4_16_1_out_14, decoder4_16_1_out_15, decoder4_16_1_out_16, decoder4_16_1_out_17, decoder4_16_1_out_19, decoder4_16_1_out_20);
  or or_3 (out_7, decoder4_16_1_out_5, decoder4_16_1_out_7, decoder4_16_1_out_8, decoder4_16_1_out_10, decoder4_16_1_out_11, decoder4_16_1_out_12, decoder4_16_1_out_13, decoder4_16_1_out_14, decoder4_16_1_out_15, decoder4_16_1_out_17, decoder4_16_1_out_19, decoder4_16_1_out_20);
  or or_4 (out_8, decoder4_16_1_out_5, decoder4_16_1_out_6, decoder4_16_1_out_7, decoder4_16_1_out_8, decoder4_16_1_out_9, decoder4_16_1_out_12, decoder4_16_1_out_13, decoder4_16_1_out_14, decoder4_16_1_out_15, decoder4_16_1_out_18);
  or or_5 (out_9, decoder4_16_1_out_5, decoder4_16_1_out_7, decoder4_16_1_out_11, decoder4_16_1_out_13, decoder4_16_1_out_20, decoder4_16_1_out_15, decoder4_16_1_out_16, decoder4_16_1_out_17, decoder4_16_1_out_18, decoder4_16_1_out_19);
  or or_6 (out_10, decoder4_16_1_out_5, decoder4_16_1_out_7, decoder4_16_1_out_8, decoder4_16_1_out_10, decoder4_16_1_out_11, decoder4_16_1_out_13, decoder4_16_1_out_14, decoder4_16_1_out_16, decoder4_16_1_out_17, decoder4_16_1_out_18, decoder4_16_1_out_19);
  or or_7 (out_11, decoder4_16_1_out_5, decoder4_16_1_out_6, decoder4_16_1_out_8, decoder4_16_1_out_9, decoder4_16_1_out_10, decoder4_16_1_out_11, decoder4_16_1_out_12, decoder4_16_1_out_13, decoder4_16_1_out_14, decoder4_16_1_out_15, decoder4_16_1_out_16, decoder4_16_1_out_18);
  _7_Segment_Display u_7_segment_display_1 (
    .g(out_5), .f(out_6), .a(out_7), .b(out_8), .e(out_9), .d(out_10), .c(out_11));  // open: dp
  Button button_1 (.out(button_1_out));
  Button button_2 (.out(button_2_out));
  Button button_3 (.out(button_3_out));
  Button button_4 (.out(button_4_out));
  _7_Segment_Display u_7_segment_display_2 (
    .g(button_4_out), .f(button_3_out), .a(button_2_out), .b(button_1_out), .e(button_5_out),
    .d(button_6_out), .c(button_7_out), .dp(button_8_out));
  Button button_5 (.out(button_5_out));
  Button button_6 (.out(button_6_out));
  Button button_7 (.out(button_7_out));
  Button button_8 (.out(button_8_out));

  // Notes on the sheet:
  //    0
  //   1
  //   2
  //   3
  //   4
  //   5
  //   6
  //   7
  //   8
  //   9
  //   A
  //   b
  //   C
  //   d
  //   E
  //   F
endmodule

module halfadder (
  input  in_1,
  input  in_2,
  output out_3,
  output out_4
);

  xor xor_1 (out_3, in_1, in_2);
  and and_1 (out_4, in_1, in_2);

  // Notes on the sheet:
  //   S
  //   C
endmodule

module fulladder_36 (
  input  in_1,
  input  in_2,
  input  in_3,
  output Sum,
  output Count
);

  wire halfadder_1_out_3, halfadder_1_out_4, halfadder_2_out_4;

  halfadder halfadder_1 (.in_1(in_1), .in_2(in_2), .out_3(halfadder_1_out_3), .out_4(halfadder_1_out_4));
  halfadder halfadder_2 (.in_1(halfadder_1_out_3), .in_2(in_3), .out_3(Sum), .out_4(halfadder_2_out_4));
  or or_1 (Count, halfadder_2_out_4, halfadder_1_out_4);

  // Notes on the sheet:
  //   But this is not a #T(36) fulladder, this is just a fulladder made of two  halfadder
endmodule

module counter_4bits (
  input  in_1,
  input  in_2
);

  wire d_ff_rst_1_out_4, d_ff_rst_2_out_4, d_ff_rst_3_out_4, d_ff_rst_4_out_4, decoder_7segments_i_1_out_5,
       decoder_7segments_i_1_out_6, decoder_7segments_i_1_out_7, decoder_7segments_i_1_out_8,
       decoder_7segments_i_1_out_9, decoder_7segments_i_1_out_10, decoder_7segments_i_1_out_11,
       fulladder_36_1_count, fulladder_36_1_sum, fulladder_36_2_count, fulladder_36_2_sum,
       fulladder_36_3_count, fulladder_36_3_sum, fulladder_36_4_sum;

  fulladder_36 fulladder_36_1 (
    .in_1(d_ff_rst_1_out_4), .in_2(1'b1), .in_3(1'b0), .Sum(fulladder_36_1_sum), .Count(fulladder_36_1_count));
  fulladder_36 fulladder_36_2 (
    .in_1(d_ff_rst_2_out_4), .in_2(1'b0), .in_3(fulladder_36_1_count), .Sum(fulladder_36_2_sum),
    .Count(fulladder_36_2_count));
  fulladder_36 fulladder_36_3 (
    .in_1(d_ff_rst_3_out_4), .in_2(1'b0), .in_3(fulladder_36_2_count), .Sum(fulladder_36_3_sum),
    .Count(fulladder_36_3_count));
  fulladder_36 fulladder_36_4 (
    .in_1(d_ff_rst_4_out_4), .in_2(1'b0), .in_3(fulladder_36_3_count), .Sum(fulladder_36_4_sum));  // open: Count
  D_FF_rst d_ff_rst_1 (.in_1(in_1), .in_2(fulladder_36_1_sum), .in_3(in_2), .out_4(d_ff_rst_1_out_4));
  D_FF_rst d_ff_rst_2 (.in_1(in_1), .in_2(fulladder_36_2_sum), .in_3(in_2), .out_4(d_ff_rst_2_out_4));
  D_FF_rst d_ff_rst_3 (.in_1(in_1), .in_2(fulladder_36_3_sum), .in_3(in_2), .out_4(d_ff_rst_3_out_4));
  D_FF_rst d_ff_rst_4 (.in_1(in_1), .in_2(fulladder_36_4_sum), .in_3(in_2), .out_4(d_ff_rst_4_out_4));
  decoder_7segments_i decoder_7segments_i_1 (
    .in_1(d_ff_rst_1_out_4), .in_2(d_ff_rst_2_out_4), .in_3(d_ff_rst_3_out_4), .in_4(d_ff_rst_4_out_4),
    .out_5(decoder_7segments_i_1_out_5), .out_6(decoder_7segments_i_1_out_6),
    .out_7(decoder_7segments_i_1_out_7), .out_8(decoder_7segments_i_1_out_8),
    .out_9(decoder_7segments_i_1_out_9), .out_10(decoder_7segments_i_1_out_10),
    .out_11(decoder_7segments_i_1_out_11));
  _7_Segment_Display u_7_segment_display_1 (
    .g(decoder_7segments_i_1_out_5), .f(decoder_7segments_i_1_out_6), .a(decoder_7segments_i_1_out_7),
    .b(decoder_7segments_i_1_out_8), .e(decoder_7segments_i_1_out_9), .d(decoder_7segments_i_1_out_10),
    .c(decoder_7segments_i_1_out_11));  // open: dp
endmodule

module immidiate_expansion (
  input  [3:0] in_1,
  output [7:0] out_2
);


  assign out_2 = {4'b0000, in_1};
endmodule

module small_and (
  input  in_1,
  input  in_2,
  output out_3
);

  and and_1 (out_3, in_1, in_2);
endmodule

module halfadder_1 (
  input  in_1,
  input  in_2,
  output out_3,
  output out_4
);

  xor xor_1 (out_3, in_1, in_2);
  and and_1 (out_4, in_1, in_2);

  // Notes on the sheet:
  //   S
  //   C
endmodule

module SR_Latch_1 (
  input  in_1,
  input  in_2,
  output Q,
  output Q_
);

  wire dipswitch_1_sw1, dipswitch_1_sw2, nor_3_out, nor_4_out;

  DipSwitch dipswitch_1 (.sw1(dipswitch_1_sw1), .sw2(dipswitch_1_sw2));  // open: sw3, sw4, sw5, sw6, sw7, sw8
  nor nor_1 (Q, in_1, Q_);
  nor nor_2 (Q_, Q, in_2);
  nor nor_3 (nor_3_out, dipswitch_1_sw1, nor_4_out);
  nor nor_4 (nor_4_out, nor_3_out, dipswitch_1_sw1);

  // Notes on the sheet:
  //   Q
  //   Q_
endmodule

module D_Latch_1 (
  input  in_1,
  input  in_2,
  output out_3
);

  wire and_1_out, and_2_out, and_3_out, and_4_out, and_5_out, not_1_out, not_2_out, not_3_out, or_1_out,
       undriven, undriven_2, undriven_3, undriven_4, xor_1_out;

  or or_1 (or_1_out, undriven, and_5_out);
  not not_1 (not_1_out, or_1_out);
  not not_2 (not_2_out, in_1);
  not not_3 (not_3_out, not_1_out);
  and and_1 (and_1_out, in_1, in_2);
  and and_2 (and_2_out, in_2, not_2_out);
  and and_3 (and_3_out, not_1_out, undriven_3);
  and and_4 (and_4_out, undriven_3, not_3_out);
  SR_Latch sr_latch_1 (.in_2(and_1_out));  // open: in_1, out_3
  SR_Latch sr_latch_2 (.in_2(and_3_out));  // open: in_1, out_3
  xor xor_1 (xor_1_out, undriven_2, undriven_4);
  and and_5 (and_5_out, xor_1_out, undriven_4);

  // Notes on the sheet:
  //   RST
  //   RST
  //   Q
  //   Q
endmodule

module D_FF_rst_1 (
  input  in_1,
  input  in_2,
  input  in_3,
  output out_4
);

  wire and_1_out, d_latch_1_out_3, not_1_out, not_2_out;

  not not_1 (not_1_out, in_1);
  not not_2 (not_2_out, in_3);
  and and_1 (and_1_out, not_1_out, in_2);
  D_Latch d_latch_1 (.in_2(not_2_out), .in_1(and_1_out), .out_3(d_latch_1_out_3));
  D_Latch d_latch_2 (.in_2(in_3), .in_1(d_latch_1_out_3), .out_3(out_4));
endmodule

module counter_8bits (
  input  in_1,
  input  in_2,
  output [7:0] out_3
);

  wire fulladder_36_1_count, fulladder_36_1_sum, fulladder_36_2_count, fulladder_36_2_sum,
       fulladder_36_3_count, fulladder_36_3_sum, fulladder_36_4_count, fulladder_36_4_sum,
       fulladder_36_5_count, fulladder_36_5_sum, fulladder_36_6_count, fulladder_36_6_sum,
       fulladder_36_7_sum, fulladder_36_8_sum;

  fulladder_36 fulladder_36_1 (
    .in_1(out_3[0]), .in_2(1'b1), .in_3(1'b0), .Sum(fulladder_36_1_sum), .Count(fulladder_36_1_count));
  fulladder_36 fulladder_36_2 (
    .in_1(out_3[1]), .in_2(1'b0), .in_3(fulladder_36_1_count), .Sum(fulladder_36_2_sum),
    .Count(fulladder_36_2_count));
  fulladder_36 fulladder_36_3 (
    .in_1(out_3[2]), .in_2(1'b0), .in_3(fulladder_36_2_count), .Sum(fulladder_36_3_sum),
    .Count(fulladder_36_3_count));
  fulladder_36 fulladder_36_4 (
    .in_1(out_3[3]), .in_2(1'b0), .in_3(fulladder_36_3_count), .Sum(fulladder_36_4_sum),
    .Count(fulladder_36_4_count));
  fulladder_36 fulladder_36_5 (
    .in_1(out_3[4]), .in_2(1'b0), .in_3(fulladder_36_4_count), .Sum(fulladder_36_5_sum),
    .Count(fulladder_36_5_count));
  fulladder_36 fulladder_36_6 (
    .in_1(out_3[5]), .in_2(1'b0), .in_3(fulladder_36_5_count), .Sum(fulladder_36_6_sum),
    .Count(fulladder_36_6_count));
  fulladder_36 fulladder_36_7 (
    .in_1(out_3[6]), .in_2(1'b0), .in_3(fulladder_36_6_count), .Sum(fulladder_36_7_sum), .Count(out_3[7]));
  fulladder_36 fulladder_36_8 (.in_1(out_3[7]), .in_2(1'b0), .in_3(out_3[7]), .Sum(fulladder_36_8_sum));  // open: Count
  D_FF_rst d_ff_rst_1 (.in_1(in_1), .in_2(fulladder_36_1_sum), .in_3(in_2), .out_4(out_3[0]));
  D_FF_rst d_ff_rst_2 (.in_1(in_1), .in_2(fulladder_36_2_sum), .in_3(in_2), .out_4(out_3[1]));
  D_FF_rst d_ff_rst_3 (.in_1(in_1), .in_2(fulladder_36_3_sum), .in_3(in_2), .out_4(out_3[2]));
  D_FF_rst d_ff_rst_4 (.in_1(in_1), .in_2(fulladder_36_4_sum), .in_3(in_2), .out_4(out_3[3]));
  D_FF_rst d_ff_rst_5 (.in_1(in_1), .in_2(fulladder_36_5_sum), .in_3(in_2), .out_4(out_3[4]));
  D_FF_rst d_ff_rst_6 (.in_1(in_1), .in_2(fulladder_36_6_sum), .in_3(in_2), .out_4(out_3[5]));
  D_FF_rst d_ff_rst_7 (.in_1(in_1), .in_2(fulladder_36_7_sum), .in_3(in_2), .out_4(out_3[6]));
  D_FF_rst d_ff_rst_8 (.in_1(in_1), .in_2(fulladder_36_8_sum), .in_3(in_2), .out_4(out_3[7]));
endmodule
